# Fritzing sketch Wiring_UNI-Sen-Current-Sensor (saved by Fritzing 0.9.3b)
circuit board: 18.8674cm x 10.2815cm

parts:
  Bauteil1 = Arduino Pro Mini v13
  0x4A = Analog Digital converter ADS1115 with I2C Interface
  S1 = Pushbutton [part_number=Config package="[THT]"]
  0x4B = Analog Digital converter ADS1115 with I2C Interface
  U1 = CC1101 [part_number=CC1101]
  J3 = AVR ISP 6 Pin [package=2x3_lock]
  230V_AC_/_5V_DC = AC-05-03
  R1 = Resistor [tolerance=±5% resistance=330 package=THT]
  SW2 = DIP SWITCH [package=dipswitch-02]
  SW3 = DIP SWITCH [package=dipswitch-02]
  LED = smd LED [color="Green (570nm)" package="0805 [SMD]"]
  LED4 = smd LED [color="Red (635nm)" package="0805 [SMD]"]
  R2 = Resistor [tolerance=±5% resistance=330 package=THT]
  L1 = sct-013 [part_number=sct-013 package="4Ucon 08780 [THT]"]
  L2 = sct-013 [part_number=sct-013 package="4Ucon 08780 [THT]"]
  L3 = sct-013 [part_number=sct-013 package="4Ucon 08780 [THT]"]

nets:
  VDD: Bauteil1.VCC, 0x4A.VDD, 0x4B.VDD, U1.1
  N1: Bauteil1.A4, Bauteil1.A5
  N2: Bauteil1.RAW, J3.2, 230V_AC_/_5V_DC.pin_3
  N3: Bauteil1.GND, Bauteil1.D8, S1.Pin_1, S1.Pin_2, S1.Pin_3, S1.Pin_4, U1.2, J3.6, 230V_AC_/_5V_DC.pin_4
  N4: Bauteil1.RESET, SW3.2
  N5: Bauteil1.D13/SCK, U1.4, SW2.2
  N6: Bauteil1.D12/MISO, U1.5, SW3.1
  N7: Bauteil1.D11_PWM/MOSI, U1.3, SW2.1
  N8: Bauteil1.D10_PWM/SS, U1.8
  N9: Bauteil1.D6_PWM, J3.5, SW3.3
  N10: Bauteil1.D5_PWM, R2.Pin_0
  N11: Bauteil1.D4, R1.Pin_0
  N12: Bauteil1.D2, U1.7
  GND: 0x4A.GND, 0x4B.GND
  N13: 0x4A.SCL, 0x4B.SCL, 0x4B.ADDR, J3.3, SW2.3
  N14: 0x4A.SDA, 0x4A.ADDR, 0x4B.SDA, J3.4, SW2.4
  N15: 0x4A.A0, L3.pin_0
  N16: 0x4A.A1, L3.pin_1
  N17: 0x4B.A0, L1.pin_0
  N18: 0x4B.A1, L1.pin_1
  N19: 0x4B.A2, L2.pin_0
  N20: 0x4B.A3, L2.pin_1
  N21: J3.1, SW3.4
  N22: R1.Pin_1, LED.anode
  N23: LED4.anode, R2.Pin_1

custom parts:
  Analog Digital converter ADS1115 with I2C Interface: Our AZ-Delivery ADS1115 is an analog-to-digital converter with 16 bit resolution and I2C interface for easy control of up to 4 analog channels. So you can finally operate and evaluate analog sensors on your Raspberry or ESP8266 and ESP32. Due to the wide voltage range between 2V and 5V the converter is suitable for nearly all microcontrollers. The I2C address can be adjusted via executed pins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
  AC-05-03: AC-DC 220V to 5V Step-Down Power Supply Module
  sct-013: sct-013 Current transformer. The pcb footprint is from the 3.5mm stereo jack (as the sensor comes with a 3.5 mm stero plug).
